# Fritzing sketch output_stage (saved by Fritzing 0.9.3b)
breadboards: 1

parts:
  U1 = 2.5mm Audio Jack [package=stereojack2.5mm_specia_pogopins]
  C1 = Electrolytic Capacitor [capacitance=1µF package="100 mil [THT, electrolytic]"]
  C2 = Ceramic Capacitor [capacitance=4.7µF package="100 mil [THT, multilayer]"]
  R2 = Resistor [tolerance=±5% resistance=1k package=THT]
  U2 = 2.5mm Audio Jack [package=stereojack2.5mm_specia_pogopins]
  R3 = Resistor [tolerance=±5% resistance=100k package=THT]

nets:
  GND: U1.SLEEVE, C2.0, R2.Pin_0, U2.SLEEVE, R3.Pin_0
  N1: U1.RIGHT, C1.-, R3.Pin_1
  N2: C1.+, C2.1, R2.Pin_1, U2.RIGHT
